# Fritzing sketch Circuit Layout (saved by Fritzing 0.7.10b)
breadboards: 1

parts:
  Arduino1 = Arduino
  LED1 = LED - 5mm [color="Green (565nm)" package="5 mm [THT]"]
  R1 = Resistor [tolerance=±5% resistance=470 package=THT]
  R2 = Resistor [tolerance=±5% resistance=470 package=THT]
  LED2 = LED - 5mm [color="Green (565nm)" package="5 mm [THT]"]
  R3 = Resistor [tolerance=±5% resistance=470 package=THT]
  LED3 = LED - 5mm [color="Green (565nm)" package="5 mm [THT]"]
  R4 = Resistor [tolerance=±5% resistance=470 package=THT]
  LED4 = LED - 5mm [color="Green (565nm)" package="5 mm [THT]"]
  R5 = Resistor [tolerance=±5% resistance=470 package=THT]
  LED5 = LED - 5mm [color="Green (565nm)" package="5 mm [THT]"]
  R6 = Resistor [tolerance=±5% resistance=470 package=THT]
  LED6 = LED - 5mm [color="Green (565nm)" package="5 mm [THT]"]
  R7 = Resistor [tolerance=±5% resistance=470 package=THT]
  LED7 = LED - 5mm [color="Green (565nm)" package="5 mm [THT]"]
  R8 = Resistor [tolerance=±5% resistance=470 package=THT]
  LED8 = LED - 5mm [color="Green (565nm)" package="5 mm [THT]"]
  R9 = Resistor [tolerance=±5% resistance=470 package=THT]
  LED9 = LED - 5mm [color="Green (565nm)" package="5 mm [THT]"]
  R10 = Resistor [tolerance=±5% resistance=470 package=THT]
  R13 = Resistor [tolerance=±5% resistance=470 package=THT]
  R14 = Resistor [tolerance=±5% resistance=470 package=THT]
  R15 = Resistor [tolerance=±5% resistance=470 package=THT]
  R16 = Resistor [tolerance=±5% resistance=470 package=THT]
  R17 = Resistor [tolerance=±5% resistance=470 package=THT]
  R18 = Resistor [tolerance=±5% resistance=470 package=THT]
  LED12 = LED - 5mm [color="Green (565nm)" package="5 mm [THT]"]
  LED15 = LED - 5mm [color="Green (565nm)" package="5 mm [THT]"]
  LED14 = LED - 5mm [color="Green (565nm)" package="5 mm [THT]"]
  LED13 = LED - 5mm [color="Green (565nm)" package="5 mm [THT]"]
  LED10 = LED - 5mm [color="Green (565nm)" package="5 mm [THT]"]
  LED11 = LED - 5mm [color="Green (565nm)" package="5 mm [THT]"]
  LED16 = LED - 5mm [color="Green (565nm)" package="5 mm [THT]"]
  VCC1 = Battery

nets:
  N1: Arduino1.D13, LED12.anode
  N2: Arduino1.D12, LED11.anode
  N3: Arduino1.D11, LED10.anode
  N4: Arduino1.D10, LED9.anode
  N5: Arduino1.D9, LED8.anode
  N6: Arduino1.D8, LED7.anode
  N7: Arduino1.D7, LED6.anode
  N8: Arduino1.D6, LED5.anode
  N9: Arduino1.D5, LED4.anode
  N10: Arduino1.D4, LED3.anode
  N11: Arduino1.D3, LED2.anode
  N12: Arduino1.D2, LED1.anode
  N13: Arduino1.GND, R1.Pin_1, R2.Pin_1, R3.Pin_1, R4.Pin_1, R5.Pin_1, R6.Pin_1, R7.Pin_1, R8.Pin_1, R9.Pin_1, R10.Pin_1, R13.Pin_1, R14.Pin_1, R15.Pin_1, R16.Pin_1, R17.Pin_1, R18.Pin_1, VCC1.-
  N14: Arduino1.VIN, VCC1.+
  N15: Arduino1.A0, LED13.anode
  N16: Arduino1.A1, LED14.anode
  N17: Arduino1.A2, LED15.anode
  N18: Arduino1.A3, LED16.anode
  N19: LED1.cathode, R1.Pin_0
  N20: R2.Pin_0, LED2.cathode
  N21: R3.Pin_0, LED3.cathode
  N22: R4.Pin_0, LED4.cathode
  N23: R5.Pin_0, LED5.cathode
  N24: R6.Pin_0, LED6.cathode
  N25: R7.Pin_0, LED7.cathode
  N26: R8.Pin_0, LED8.cathode
  N27: R9.Pin_0, LED9.cathode
  N28: R10.Pin_0, LED13.cathode
  N29: R13.Pin_0, LED11.cathode
  N30: R14.Pin_0, LED15.cathode
  N31: R15.Pin_0, LED16.cathode
  N32: R16.Pin_0, LED10.cathode
  N33: R17.Pin_0, LED12.cathode
  N34: R18.Pin_0, LED14.cathode
